// Logisim project CUSTOM_CPU_DESIGN.circ as structural Verilog
module _2x4_DECODER (
  input  a,
  input  b,
  output out_3,
  output out_4,
  output out_5,
  output out_6
);

  wire not_1_out, not_2_out;

  not not_1 (not_1_out, a);
  not not_2 (not_2_out, b);
  and and_1 (out_3, b, a);
  and and_2 (out_4, not_2_out, a);
  and and_3 (out_5, b, not_1_out);
  and and_4 (out_6, not_2_out, not_1_out);
endmodule

module _3x8_DECODER (
  input  a,
  input  b,
  input  c,
  output [7:0] out_4
);

  wire not_1_out, not_2_out, not_3_out;

  not not_1 (not_1_out, a);
  not not_2 (not_2_out, b);
  not not_3 (not_3_out, c);
  and and_1 (out_4[0], not_1_out, not_2_out, not_3_out);
  and and_2 (out_4[1], a, not_2_out, not_3_out);
  and and_3 (out_4[2], not_1_out, b, not_3_out);
  and and_4 (out_4[3], a, b, not_3_out);
  and and_5 (out_4[4], not_1_out, not_2_out, c);
  and and_6 (out_4[5], a, not_2_out, c);
  and and_7 (out_4[6], not_1_out, b, c);
  and and_8 (out_4[7], a, b, c);
endmodule

module _4x16_DECODER (
  input  [3:0] in_1,
  output out_2,
  output out_3,
  output out_4,
  output out_5,
  output out_6,
  output out_7,
  output out_8,
  output out_9,
  output out_10,
  output out_11,
  output out_12,
  output out_13,
  output out_14,
  output out_15,
  output out_16,
  output out_17
);

  wire not_1_out, not_2_out, not_3_out, not_4_out;

  not not_1 (not_1_out, in_1[0]);
  not not_2 (not_2_out, in_1[1]);
  not not_3 (not_3_out, in_1[2]);
  not not_4 (not_4_out, in_1[3]);
  and and_1 (out_2, not_4_out, not_3_out, not_2_out, not_1_out);
  and and_2 (out_3, not_4_out, not_3_out, not_2_out, in_1[0]);
  and and_3 (out_4, not_4_out, not_3_out, in_1[1], not_1_out);
  and and_4 (out_5, in_1[0], in_1[1], not_3_out, not_4_out);
  and and_5 (out_6, not_4_out, in_1[2], not_2_out, not_1_out);
  and and_6 (out_7, not_4_out, in_1[2], not_2_out, in_1[0]);
  and and_7 (out_8, not_4_out, in_1[2], in_1[1], not_1_out);
  and and_8 (out_9, not_4_out, in_1[2], in_1[1], in_1[0]);
  and and_9 (out_10, in_1[3], not_3_out, not_2_out, not_1_out);
  and and_10 (out_11, in_1[3], not_3_out, not_2_out, in_1[0]);
  and and_11 (out_12, in_1[3], not_3_out, in_1[1], not_1_out);
  and and_12 (out_13, in_1[3], not_3_out, in_1[1], in_1[0]);
  and and_13 (out_14, in_1[2], in_1[2], not_2_out, not_1_out);
  and and_14 (out_15, in_1[3], in_1[2], not_2_out, in_1[0]);
  and and_15 (out_16, in_1[3], in_1[2], in_1[1], not_1_out);
  and and_16 (out_17, in_1[3], in_1[2], in_1[1], in_1[0]);
endmodule

module CPU_MEM_1 (
  input  s,
  input  e,
  output q
);

  wire nand_1_out, nand_2_out, nand_4_out;

  nand nand_1 (nand_1_out, s, e);
  nand nand_2 (nand_2_out, nand_1_out, e);
  nand nand_3 (q, nand_1_out, nand_4_out);
  nand nand_4 (nand_4_out, q, nand_2_out);

  // Notes on the sheet:
  //   One bit memory Cell
endmodule

module CPU_MEM_8 (
  input  [7:0] i,
  input  s,
  output [7:0] o
);

  CPU_MEM_1 cpu_mem_1_1 (.s(i[0]), .e(s), .q(o[0]));
  CPU_MEM_1 cpu_mem_1_2 (.s(i[1]), .e(s), .q(o[1]));
  CPU_MEM_1 cpu_mem_1_3 (.s(i[2]), .e(s), .q(o[2]));
  CPU_MEM_1 cpu_mem_1_4 (.s(i[3]), .e(s), .q(o[3]));
  CPU_MEM_1 cpu_mem_1_5 (.s(i[4]), .e(s), .q(o[4]));
  CPU_MEM_1 cpu_mem_1_6 (.s(i[5]), .e(s), .q(o[5]));
  CPU_MEM_1 cpu_mem_1_7 (.s(i[6]), .e(s), .q(o[6]));
  CPU_MEM_1 cpu_mem_1_8 (.s(i[7]), .e(s), .q(o[7]));
endmodule

module CPU_ENABLE (
  input  [7:0] i,
  input  e,
  output [7:0] o
);

  wire and_1_out, and_2_out, and_3_out, and_4_out, and_5_out, and_6_out, and_7_out, and_8_out;

  and and_1 (and_1_out, i[0], e);
  and and_2 (and_2_out, i[1], e);
  and and_3 (and_3_out, i[2], e);
  and and_4 (and_4_out, i[3], e);
  and and_5 (and_5_out, i[4], e);
  and and_6 (and_6_out, i[5], e);
  and and_7 (and_7_out, i[6], e);
  and and_8 (and_8_out, i[7], e);
  assign o[0] = e ? and_1_out : 1'bz;  // Controlled_Buffer controlled_buffer_1
  assign o[1] = e ? and_2_out : 1'bz;  // Controlled_Buffer controlled_buffer_2
  assign o[2] = e ? and_3_out : 1'bz;  // Controlled_Buffer controlled_buffer_3
  assign o[3] = e ? and_4_out : 1'bz;  // Controlled_Buffer controlled_buffer_4
  assign o[4] = e ? and_5_out : 1'bz;  // Controlled_Buffer controlled_buffer_5
  assign o[5] = e ? and_6_out : 1'bz;  // Controlled_Buffer controlled_buffer_6
  assign o[6] = e ? and_7_out : 1'bz;  // Controlled_Buffer controlled_buffer_7
  assign o[7] = e ? and_8_out : 1'bz;  // Controlled_Buffer controlled_buffer_8
endmodule

module CPU_REG_8 (
  input  [7:0] i,
  input  s,
  input  e,
  output [7:0] out_4,
  output [7:0] o
);

  wire [7:0] cpu_enable_1_o;

  CPU_MEM_8 cpu_mem_8_1 (.i(i), .o(out_4), .s(s));
  CPU_ENABLE cpu_enable_1 (.i(out_4), .o(cpu_enable_1_o), .e(e));
  assign o = e ? cpu_enable_1_o : 8'bz;  // Controlled_Buffer controlled_buffer_1
endmodule

module CPU_REG_BYTE (
  input  [7:0] in_1,
  input  RESET,
  input  h,
  input  v,
  input  s,
  input  e,
  output [7:0] out_7,
  output [7:0] \reg 
);

  wire and_1_out, and_2_out, and_3_out, or_1_out;
  wire [7:0] cpu_reg_8_1_o;

  and and_1 (and_1_out, h, v);
  and and_2 (and_2_out, and_1_out, s);
  and and_3 (and_3_out, and_1_out, e);
  or or_1 (or_1_out, RESET, and_2_out);
  assign out_7 = and_3_out ? cpu_reg_8_1_o : 8'bz;  // Controlled_Buffer controlled_buffer_1
  CPU_REG_8 cpu_reg_8_1 (.i(in_1), .o(cpu_reg_8_1_o), .s(or_1_out), .e(and_3_out), .out_4(\reg ));

  // Notes on the sheet:
  //   i
  //   o
endmodule

module RAM_32 (
  input  reset,
  input  [7:0] i,
  input  [7:0] address,
  input  s,
  input  e,
  output [7:0] o,
  output [7:0] _0,
  output [7:0] _1,
  output [7:0] _2,
  output [7:0] _3,
  output [7:0] _4,
  output [7:0] _5,
  output [7:0] _6,
  output [7:0] _7,
  output [7:0] _8,
  output [7:0] _9,
  output [7:0] _10,
  output [7:0] _11,
  output [7:0] _12,
  output [7:0] _13,
  output [7:0] _14,
  output [7:0] _15,
  output [7:0] _16,
  output [7:0] _17,
  output [7:0] _18,
  output [7:0] _19,
  output [7:0] _20,
  output [7:0] _21,
  output [7:0] _22,
  output [7:0] _23,
  output [7:0] _24,
  output [7:0] _25,
  output [7:0] _26,
  output [7:0] _27,
  output [7:0] _28,
  output [7:0] _29,
  output [7:0] _30,
  output [7:0] _31
);

  wire n2x4_decoder_1_out_3, n2x4_decoder_1_out_4, n2x4_decoder_1_out_5, n2x4_decoder_1_out_6;
  wire [7:0] cpu_reg_byte_1_out_7, n3x8_decoder_1_out_4;

  _3x8_DECODER u_3x8_decoder_1 (.out_4(n3x8_decoder_1_out_4), .a(address[2]), .b(address[3]), .c(address[4]));
  assign o = e ? cpu_reg_byte_1_out_7 : 8'bz;  // Controlled_Buffer controlled_buffer_1
  _2x4_DECODER u_2x4_decoder_1 (
    .out_3(n2x4_decoder_1_out_3), .out_4(n2x4_decoder_1_out_4), .out_5(n2x4_decoder_1_out_5),
    .out_6(n2x4_decoder_1_out_6), .a(address[0]), .b(address[1]));
  CPU_REG_BYTE cpu_reg_byte_1 (
    .in_1(i), .h(n3x8_decoder_1_out_4[0]), .v(n2x4_decoder_1_out_6), .out_7(cpu_reg_byte_1_out_7),
    .\reg (_0), .RESET(reset), .s(s), .e(e));
  CPU_REG_BYTE cpu_reg_byte_2 (
    .in_1(i), .h(n3x8_decoder_1_out_4[1]), .v(n2x4_decoder_1_out_6), .out_7(cpu_reg_byte_1_out_7),
    .\reg (_4), .RESET(reset), .s(s), .e(e));
  CPU_REG_BYTE cpu_reg_byte_3 (
    .in_1(i), .h(n3x8_decoder_1_out_4[2]), .v(n2x4_decoder_1_out_6), .out_7(cpu_reg_byte_1_out_7),
    .\reg (_8), .RESET(reset), .s(s), .e(e));
  CPU_REG_BYTE cpu_reg_byte_4 (
    .in_1(i), .h(n3x8_decoder_1_out_4[3]), .v(n2x4_decoder_1_out_6), .out_7(cpu_reg_byte_1_out_7),
    .\reg (_12), .RESET(reset), .s(s), .e(e));
  CPU_REG_BYTE cpu_reg_byte_5 (
    .in_1(i), .h(n3x8_decoder_1_out_4[4]), .v(n2x4_decoder_1_out_6), .out_7(cpu_reg_byte_1_out_7),
    .\reg (_16), .RESET(reset), .s(s), .e(e));
  CPU_REG_BYTE cpu_reg_byte_6 (
    .in_1(i), .h(n3x8_decoder_1_out_4[5]), .v(n2x4_decoder_1_out_6), .out_7(cpu_reg_byte_1_out_7),
    .\reg (_20), .RESET(reset), .s(s), .e(e));
  CPU_REG_BYTE cpu_reg_byte_7 (
    .in_1(i), .h(n3x8_decoder_1_out_4[6]), .v(n2x4_decoder_1_out_6), .out_7(cpu_reg_byte_1_out_7),
    .\reg (_24), .RESET(reset), .s(s), .e(e));
  CPU_REG_BYTE cpu_reg_byte_8 (
    .in_1(i), .h(n3x8_decoder_1_out_4[7]), .v(n2x4_decoder_1_out_6), .out_7(cpu_reg_byte_1_out_7),
    .\reg (_28), .RESET(reset), .s(s), .e(e));
  CPU_REG_BYTE cpu_reg_byte_9 (
    .in_1(i), .h(n3x8_decoder_1_out_4[0]), .v(n2x4_decoder_1_out_5), .out_7(cpu_reg_byte_1_out_7),
    .\reg (_1), .RESET(reset), .s(s), .e(e));
  CPU_REG_BYTE cpu_reg_byte_10 (
    .in_1(i), .h(n3x8_decoder_1_out_4[1]), .v(n2x4_decoder_1_out_5), .out_7(cpu_reg_byte_1_out_7),
    .\reg (_5), .RESET(reset), .s(s), .e(e));
  CPU_REG_BYTE cpu_reg_byte_11 (
    .in_1(i), .h(n3x8_decoder_1_out_4[2]), .v(n2x4_decoder_1_out_5), .out_7(cpu_reg_byte_1_out_7),
    .\reg (_9), .RESET(reset), .s(s), .e(e));
  CPU_REG_BYTE cpu_reg_byte_12 (
    .in_1(i), .h(n3x8_decoder_1_out_4[3]), .v(n2x4_decoder_1_out_5), .out_7(cpu_reg_byte_1_out_7),
    .\reg (_13), .RESET(reset), .s(s), .e(e));
  CPU_REG_BYTE cpu_reg_byte_13 (
    .in_1(i), .h(n3x8_decoder_1_out_4[4]), .v(n2x4_decoder_1_out_5), .out_7(cpu_reg_byte_1_out_7),
    .\reg (_17), .RESET(reset), .s(s), .e(e));
  CPU_REG_BYTE cpu_reg_byte_14 (
    .in_1(i), .h(n3x8_decoder_1_out_4[5]), .v(n2x4_decoder_1_out_5), .out_7(cpu_reg_byte_1_out_7),
    .\reg (_21), .RESET(reset), .s(s), .e(e));
  CPU_REG_BYTE cpu_reg_byte_15 (
    .in_1(i), .h(n3x8_decoder_1_out_4[6]), .v(n2x4_decoder_1_out_5), .out_7(cpu_reg_byte_1_out_7),
    .\reg (_25), .RESET(reset), .s(s), .e(e));
  CPU_REG_BYTE cpu_reg_byte_16 (
    .in_1(i), .h(n3x8_decoder_1_out_4[7]), .v(n2x4_decoder_1_out_5), .out_7(cpu_reg_byte_1_out_7),
    .\reg (_29), .RESET(reset), .s(s), .e(e));
  CPU_REG_BYTE cpu_reg_byte_17 (
    .in_1(i), .h(n3x8_decoder_1_out_4[0]), .v(n2x4_decoder_1_out_4), .out_7(cpu_reg_byte_1_out_7),
    .\reg (_2), .RESET(reset), .s(s), .e(e));
  CPU_REG_BYTE cpu_reg_byte_18 (
    .in_1(i), .h(n3x8_decoder_1_out_4[1]), .v(n2x4_decoder_1_out_4), .out_7(cpu_reg_byte_1_out_7),
    .\reg (_6), .RESET(reset), .s(s), .e(e));
  CPU_REG_BYTE cpu_reg_byte_19 (
    .in_1(i), .h(n3x8_decoder_1_out_4[2]), .v(n2x4_decoder_1_out_4), .out_7(cpu_reg_byte_1_out_7),
    .\reg (_10), .RESET(reset), .s(s), .e(e));
  CPU_REG_BYTE cpu_reg_byte_20 (
    .in_1(i), .h(n3x8_decoder_1_out_4[3]), .v(n2x4_decoder_1_out_4), .out_7(cpu_reg_byte_1_out_7),
    .\reg (_14), .RESET(reset), .s(s), .e(e));
  CPU_REG_BYTE cpu_reg_byte_21 (
    .in_1(i), .h(n3x8_decoder_1_out_4[4]), .v(n2x4_decoder_1_out_4), .out_7(cpu_reg_byte_1_out_7),
    .\reg (_18), .RESET(reset), .s(s), .e(e));
  CPU_REG_BYTE cpu_reg_byte_22 (
    .in_1(i), .h(n3x8_decoder_1_out_4[5]), .v(n2x4_decoder_1_out_4), .out_7(cpu_reg_byte_1_out_7),
    .\reg (_22), .RESET(reset), .s(s), .e(e));
  CPU_REG_BYTE cpu_reg_byte_23 (
    .in_1(i), .h(n3x8_decoder_1_out_4[6]), .v(n2x4_decoder_1_out_4), .out_7(cpu_reg_byte_1_out_7),
    .\reg (_26), .RESET(reset), .s(s), .e(e));
  CPU_REG_BYTE cpu_reg_byte_24 (
    .in_1(i), .h(n3x8_decoder_1_out_4[7]), .v(n2x4_decoder_1_out_4), .out_7(cpu_reg_byte_1_out_7),
    .\reg (_30), .RESET(reset), .s(s), .e(e));
  CPU_REG_BYTE cpu_reg_byte_25 (
    .in_1(i), .h(n3x8_decoder_1_out_4[0]), .v(n2x4_decoder_1_out_3), .out_7(cpu_reg_byte_1_out_7),
    .\reg (_3), .RESET(reset), .s(s), .e(e));
  CPU_REG_BYTE cpu_reg_byte_26 (
    .in_1(i), .h(n3x8_decoder_1_out_4[1]), .v(n2x4_decoder_1_out_3), .out_7(cpu_reg_byte_1_out_7),
    .\reg (_7), .RESET(reset), .s(s), .e(e));
  CPU_REG_BYTE cpu_reg_byte_27 (
    .in_1(i), .h(n3x8_decoder_1_out_4[2]), .v(n2x4_decoder_1_out_3), .out_7(cpu_reg_byte_1_out_7),
    .\reg (_11), .RESET(reset), .s(s), .e(e));
  CPU_REG_BYTE cpu_reg_byte_28 (
    .in_1(i), .h(n3x8_decoder_1_out_4[3]), .v(n2x4_decoder_1_out_3), .out_7(cpu_reg_byte_1_out_7),
    .\reg (_15), .RESET(reset), .s(s), .e(e));
  CPU_REG_BYTE cpu_reg_byte_29 (
    .in_1(i), .h(n3x8_decoder_1_out_4[4]), .v(n2x4_decoder_1_out_3), .out_7(cpu_reg_byte_1_out_7),
    .\reg (_19), .RESET(reset), .s(s), .e(e));
  CPU_REG_BYTE cpu_reg_byte_30 (
    .in_1(i), .h(n3x8_decoder_1_out_4[5]), .v(n2x4_decoder_1_out_3), .out_7(cpu_reg_byte_1_out_7),
    .\reg (_23), .RESET(reset), .s(s), .e(e));
  CPU_REG_BYTE cpu_reg_byte_31 (
    .in_1(i), .h(n3x8_decoder_1_out_4[6]), .v(n2x4_decoder_1_out_3), .out_7(cpu_reg_byte_1_out_7),
    .\reg (_27), .RESET(reset), .s(s), .e(e));
  CPU_REG_BYTE cpu_reg_byte_32 (
    .in_1(i), .h(n3x8_decoder_1_out_4[7]), .v(n2x4_decoder_1_out_3), .out_7(cpu_reg_byte_1_out_7),
    .\reg (_31), .RESET(reset), .s(s), .e(e));
endmodule

module CPU_ADDER (
  input  Cin,
  input  a,
  input  b,
  output s,
  output Cout
);

  wire and_1_out, and_2_out, xor_1_out;

  xor xor_1 (xor_1_out, a, b);
  and and_1 (and_1_out, b, a);
  xor xor_2 (s, Cin, xor_1_out);
  and and_2 (and_2_out, Cin, xor_1_out);
  or or_1 (Cout, and_2_out, and_1_out);
endmodule

module CPU_ADDER_8 (
  input  C_in,
  input  [7:0] in_2,
  input  [7:0] in_3,
  output [7:0] out_4,
  output C_out
);

  wire cpu_adder_1_cout, cpu_adder_2_cout, cpu_adder_3_cout, cpu_adder_4_cout, cpu_adder_5_cout,
       cpu_adder_6_cout, cpu_adder_7_cout;

  CPU_ADDER cpu_adder_1 (.Cin(C_in), .a(in_2[0]), .b(in_3[0]), .s(out_4[0]), .Cout(cpu_adder_1_cout));
  CPU_ADDER cpu_adder_2 (.Cin(cpu_adder_1_cout), .a(in_2[1]), .b(in_3[1]), .s(out_4[1]), .Cout(cpu_adder_2_cout));
  CPU_ADDER cpu_adder_3 (.Cin(cpu_adder_2_cout), .a(in_2[2]), .b(in_3[2]), .s(out_4[2]), .Cout(cpu_adder_3_cout));
  CPU_ADDER cpu_adder_4 (.Cin(cpu_adder_3_cout), .a(in_2[3]), .b(in_3[3]), .s(out_4[3]), .Cout(cpu_adder_4_cout));
  CPU_ADDER cpu_adder_5 (.Cin(cpu_adder_4_cout), .a(in_2[4]), .b(in_3[4]), .s(out_4[4]), .Cout(cpu_adder_5_cout));
  CPU_ADDER cpu_adder_6 (.Cin(cpu_adder_5_cout), .a(in_2[5]), .b(in_3[5]), .s(out_4[5]), .Cout(cpu_adder_6_cout));
  CPU_ADDER cpu_adder_7 (.Cin(cpu_adder_6_cout), .a(in_2[6]), .b(in_3[6]), .s(out_4[6]), .Cout(cpu_adder_7_cout));
  CPU_ADDER cpu_adder_8 (.Cin(cpu_adder_7_cout), .a(in_2[7]), .b(in_3[7]), .s(out_4[7]), .Cout(C_out));
endmodule
