// Logisim project Design A CPU.circ as structural Verilog
module CPU_ALU (
  input  [7:0] a,
  input  [7:0] b,
  input  carry_in,
  input  x,
  input  y,
  input  z,
  output a_larger,
  output equal,
  output zero,
  output [7:0] o,
  output carry_out
);

  wire cpu_adder_8_1_c_out, cpu_and_1_p3, cpu_not_1_p2, cpu_or_1_p3, cpu_shl_1_p3, cpu_shl_1_p4,
       cpu_shr_1_p5, cpu_shr_1_p6, cpu_xor_le_8_1_p7;
  wire [7:0] cpu_adder_8_1_out_4, n3x8_decoder_1_out_4;

  // CPU_XOR_LE_8 cpu_xor_le_8_1: pin names not known; wires that end beside it: b, a, a, b, a_larger, equal, cpu_xor_le_8_1_p7
  // CPU_AND cpu_and_1: pin names not known; wires that end beside it: a, b, cpu_and_1_p3
  // CPU_SHR cpu_shr_1: pin names not known; wires that end beside it: b, a, carry_in, a, cpu_shr_1_p5, cpu_shr_1_p6
  // CPU_OR cpu_or_1: pin names not known; wires that end beside it: a, b, cpu_or_1_p3
  // CPU_NOT cpu_not_1: pin names not known; wires that end beside it: a, cpu_not_1_p2
  // CPU_SHL cpu_shl_1: pin names not known; wires that end beside it: a, carry_in, cpu_shl_1_p3, cpu_shl_1_p4
  CPU_ADDER_8 cpu_adder_8_1 (
    .in_2(a), .in_3(b), .out_4(cpu_adder_8_1_out_4), .C_in(carry_in), .C_out(cpu_adder_8_1_c_out));
  _3x8_DECODER u_3x8_decoder_1 (.out_4(n3x8_decoder_1_out_4), .a(x), .b(y), .c(z));
  // CPU_E cpu_e_1: pin names not known; wires that end beside it: cpu_xor_le_8_1_p7, n3x8_decoder_1_out_4[6], o
  // CPU_E cpu_e_2: pin names not known; wires that end beside it: cpu_or_1_p3, n3x8_decoder_1_out_4[5]
  // CPU_E cpu_e_3: pin names not known; wires that end beside it: cpu_and_1_p3, n3x8_decoder_1_out_4[4], o
  // CPU_E cpu_e_4: pin names not known; wires that end beside it: cpu_not_1_p2, n3x8_decoder_1_out_4[3], o
  // CPU_E cpu_e_5: pin names not known; wires that end beside it: cpu_shl_1_p4, n3x8_decoder_1_out_4[2], o
  // CPU_E cpu_e_6: pin names not known; wires that end beside it: cpu_shr_1_p5, n3x8_decoder_1_out_4[1], o
  // CPU_E cpu_e_7: pin names not known; wires that end beside it: cpu_adder_8_1_out_4, n3x8_decoder_1_out_4[0], o
  assign carry_out = n3x8_decoder_1_out_4[2] ? cpu_shl_1_p3 : 1'bz;  // Controlled_Buffer controlled_buffer_1
  assign carry_out = n3x8_decoder_1_out_4[1] ? cpu_shr_1_p6 : 1'bz;  // Controlled_Buffer controlled_buffer_2
  assign carry_out = n3x8_decoder_1_out_4[0] ? cpu_adder_8_1_c_out : 1'bz;  // Controlled_Buffer controlled_buffer_3
  // CPU_Z cpu_z_1: pin names not known; wires that end beside it: o, zero
endmodule
